# Fritzing sketch Final Wiring (saved by Fritzing 1.0.2b)
breadboards: 1

parts:
  Part2 = MQ-3 breakout
  Part3 = Arduino Uno (Rev3)
  Mod1 = Amica NodeMCU DEVKIT 1.0
  J1 = Piezo Speaker
  LED1 = smd LED [color="Red (633nm)" package="0603 [SMD]"]
  R1 = Resistor [tolerance=±5% resistance=220 package="1206 [SMD]"]
  R2 = Resistor [tolerance=±5% resistance=220 package="1206 [SMD]"]

nets:
  VCC: Part2.VCC, Part3.5V
  GND: Part2.GND, Part3.GND
  N1: Part2.AO, Part3.A5/SCL
  N2: Part3.D0/RX, R2.Pin_1
  N3: Part3.D1/TX, R1.Pin_1
  N4: Mod1.pin3, R1.Pin_0
  N5: Mod1.pin4, R2.Pin_0
  N6: J1.pin1, LED1.cathode
  N7: J1.pin2, LED1.anode

custom parts:
  MQ-3 breakout: Alcohol sensor is capable of detecting alcohol (ethanol) particles on itself and gives the information in digital form back to us to manipulate with it. SKU:101251 • Voltage: 5V DC • Power: max 750mW • Measurement range: 0.04-4mg/L
